// Logisim project Assignment 1.circ as structural Verilog: 1 circuit, main circuit main
module main (
  input  A,
  input  A_2,
  input  B,
  input  B_2,
  input  A_3,
  input  A_4,
  input  B_3,
  input  B_4,
  input  A_5,
  input  A_6,
  input  A_7,
  input  B_5,
  input  B_6,
  output Y___AB,
  output Y____A_B__prime,
  output Y___A_B,
  output Y___A_prime_B___B_prime_A,
  output Y___A_prime,
  output Y___A_prime_B_prime___AB,
  output Y____AB__prime
);

  and and_1 (Y___AB, A, B);
  or or_1 (Y___A_B, A_3, B_3);
  not not_1 (Y___A_prime, A_5);
  nand nand_1 (Y____AB__prime, A_7, B_6);
  nor nor_1 (Y____A_B__prime, A_2, B_2);
  xor xor_1 (Y___A_prime_B___B_prime_A, A_4, B_4);
  xnor xnor_1 (Y___A_prime_B_prime___AB, A_6, B_5);

  // Notes on the sheet:
  //   AND Gate
  //   OR Gate
  //   NOT Gate
  //   NAND Gate
  //   Name - Debarghaya Mitra            Enrollment Number - 12024052002215            Branch - CSE                Section - C                Roll No - 248
  //   Assignment - 1
  //   NOR Gate
  //   XOR Gate
  //   XNOR Gate
endmodule
