// Logisim project Assignment 10.circ as structural Verilog: 1 circuit, main circuit main
module main (
  input  B3,
  input  G3,
  input  B2,
  input  G2,
  input  B1,
  input  G1,
  input  B0,
  input  G0,
  output G3_2,
  output B3_2,
  output G2_2,
  output B2_2,
  output G1_2,
  output B1_2,
  output G0_2,
  output B0_2
);

  buf xor_1 (G3_2, B3);  // XOR_Gate
  xor xor_2 (G2_2, B2, B1);
  xor xor_3 (G1_2, B1, B0);
  xor xor_4 (B3_2, G3, B2_2);
  xor xor_5 (B2_2, G2, B1_2);
  xor xor_6 (B1_2, G1, G0);

  assign B0_2 = G0;
  assign G0_2 = B0;

  // Notes on the sheet:
  //   Binary to Gray Code
  //   Name - Debarghaya Mitra        Enrollment Number - 12024052002215        Branch - CSE        Section - C        Roll No - 248
  //   Assignment - 10
  //   Gray to Binary Code
endmodule
