// Logisim project Assignment 13.circ as structural Verilog: 1 circuit, main circuit main
module main (
  input  X,
  input  Y,
  output D1___X_prime_Y_prime,
  output D2___XY_prime,
  output D3___X_prime_Y,
  output D4___XY
);

  wire not_1_out, not_2_out;

  not not_1 (not_1_out, X);
  not not_2 (not_2_out, Y);
  and and_1 (D1___X_prime_Y_prime, not_1_out, not_2_out);
  and and_2 (D2___XY_prime, not_1_out, Y);
  and and_3 (D3___X_prime_Y, X, not_2_out);
  and and_4 (D4___XY, X, Y);

  // Notes on the sheet:
  //   Name - Debarghaya Mitra        Enrollment Number - 12024052002215        Branch - CSE        Section - C        Roll No - 248
  //   Assignment - 13
  //   2 X 4 Decoder
endmodule
