// Logisim project Assignment 17.circ as structural Verilog: 1 circuit, main circuit main
module main (
  input  A,
  input  B,
  input  C,
  input  Parity,
  output ODD___A_XNOR_B_XNOR_C_XNOR_Parity,
  output EVEN___A_XOR_B_XOR_C_XOR_Parity
);

  ExactlyOne xor_1 (.out(EVEN___A_XOR_B_XOR_C_XOR_Parity), .in0(A), .in1(B), .in2(C), .in3(Parity));
  NotExactlyOne xnor_1 (.out(ODD___A_XNOR_B_XNOR_C_XNOR_Parity), .in0(A), .in1(B), .in2(C), .in3(Parity));

  // Notes on the sheet:
  //   Name - Debarghaya Mitra        Enrollment Number - 12024052002215        Branch - CSE        Section - C        Roll No - 248
  //   Assignment - 17
  //   Parity Checker
endmodule
