// Logisim project Assignment 3.circ as structural Verilog: 1 circuit, main circuit main
module main (
  input  A,
  input  B,
  input  C,
  input  D,
  output F___A_prime_B___C_prime_D
);

  wire A_prime_B_out, A_prime_out, B_prime_out, C_prime_D_out;

  not A_prime (A_prime_out, A);
  not B_prime (B_prime_out, C);
  and A_prime_B (A_prime_B_out, A_prime_out, B);
  and C_prime_D (C_prime_D_out, B_prime_out, D);
  or or_1 (F___A_prime_B___C_prime_D, A_prime_B_out, C_prime_D_out);

  // Notes on the sheet:
  //   Assignment - 3
  //   Name - Debarghaya Mitra        Enrollment Number - 12024052002215        Branch - CSE        Section - C        Roll No - 248
endmodule
