// Logisim project Assignment 4.circ as structural Verilog: 1 circuit, main circuit main
module main (
  input  A,
  input  B,
  input  C,
  output F___C_A_prime_B_prime__AB____C_A_prime_B___B_prime_A
);

  wire and_1_out, and_2_out, xnor_1_out, xor_1_out;

  xor xor_1 (xor_1_out, B, A);
  xnor xnor_1 (xnor_1_out, B, A);
  and and_1 (and_1_out, xor_1_out, C);
  and and_2 (and_2_out, xnor_1_out, C);
  or or_1 (F___C_A_prime_B_prime__AB____C_A_prime_B___B_prime_A, and_1_out, and_2_out);

  // Notes on the sheet:
  //   A'B + B'A
  //   A'B' + AB
  //   Name - Debarghaya Mitra        Enrollment Number - 12024052002215        Branch - CSE        Section - C        Roll No - 248
  //   Assignment - 4
  //   C(A'B + B'A)
  //   C(A'B' + AB)
endmodule
