// Logisim project Assignment 7.circ as structural Verilog: 1 circuit, main circuit main
module main (
  input  A,
  input  A_2,
  input  B,
  input  B_2,
  input  A_3,
  input  A_4,
  input  B_3,
  input  B_4,
  output F___A_prime_B___AB_prime,
  output F___A_prime_B___AB_prime_2,
  output F___AB___A_prime_B_prime,
  output F___AB___A_prime_B_prime_2
);

  wire nand_1_out, nand_2_out, nand_3_out, nand_4_out, nand_5_out, nand_6_out, nand_8_out, nor_1_out,
       nor_2_out, nor_3_out, nor_4_out, nor_5_out, nor_6_out, nor_7_out;

  nand nand_1 (nand_1_out, A, B);
  nand nand_2 (nand_2_out, A_3, B_3);
  nand nand_3 (nand_3_out, A, nand_1_out);
  nand nand_4 (nand_4_out, nand_1_out, B);
  nand nand_5 (nand_5_out, A_3, nand_2_out);
  nand nand_6 (nand_6_out, nand_2_out, B_3);
  nand nand_7 (F___A_prime_B___AB_prime, nand_3_out, nand_4_out);
  nand nand_8 (nand_8_out, nand_5_out, nand_6_out);
  nand nand_9 (F___AB___A_prime_B_prime, nand_8_out, nand_8_out);
  nor nor_1 (nor_1_out, A_2, B_2);
  nor nor_2 (nor_2_out, A_2, nor_1_out);
  nor nor_3 (nor_3_out, nor_1_out, B_2);
  nor nor_4 (nor_4_out, A_4, B_4);
  nor nor_5 (nor_5_out, A_4, nor_4_out);
  nor nor_6 (nor_6_out, nor_4_out, B_4);
  nor nor_7 (nor_7_out, nor_2_out, nor_3_out);
  nor nor_8 (F___A_prime_B___AB_prime_2, nor_7_out, nor_7_out);
  nor nor_9 (F___AB___A_prime_B_prime_2, nor_5_out, nor_6_out);

  // Notes on the sheet:
  //   XOR Gate using NAND Gate
  //   XNOR Gate using NAND Gate
  //   Name - Debarghaya Mitra        Enrollment Number - 12024052002215        Branch - CSE        Section - C        Roll No - 248
  //   Assignment - 7
  //   XOR Gate using NOR Gate
  //   XNOR Gate using NOR Gate
endmodule
