// Logisim project Assignment 14.circ as structural Verilog: 1 circuit, main circuit main
module main (
  input  I0,
  input  I1,
  input  I2,
  input  I3,
  output X___I2___I3,
  output Y___I1___I3
);

  or or_1 (X___I2___I3, I3, I2);
  or or_2 (Y___I1___I3, I3, I1);

  // Notes on the sheet:
  //   Name - Debarghaya Mitra        Enrollment Number - 12024052002215        Branch - CSE        Section - C        Roll No - 248
  //   Assignment - 14
  //   4 X 2 Encoder
endmodule
