// Logisim project Assignment 15.circ as structural Verilog: 1 circuit, main circuit main
module main (
  input  I0,
  input  I1,
  input  I2,
  input  I3,
  output X___I2___I3,
  output Y___I1_I2_prime___I3,
  output V___I0___I1___I2___I3
);

  wire and_1_out, not_1_out;

  not not_1 (not_1_out, I2);
  and and_1 (and_1_out, not_1_out, I1);
  or or_1 (X___I2___I3, I3, I2);
  or or_2 (V___I0___I1___I2___I3, I0, I1, I2, I3);
  or or_3 (Y___I1_I2_prime___I3, and_1_out, I3);

  // Notes on the sheet:
  //   Name - Debarghaya Mitra        Enrollment Number - 12024052002215        Branch - CSE        Section - C        Roll No - 248
  //   Assignment - 15
  //   4 X 2 Priority Encoder
endmodule
