// Logisim project Assignment 16.circ as structural Verilog: 1 circuit, main circuit main
module main (
  input  A,
  input  B,
  input  C,
  output ODD___A_XNOR_B_XNOR_C,
  output EVEN___A_XOR_B_XOR_C
);

  ExactlyOne xor_1 (.out(EVEN___A_XOR_B_XOR_C), .in0(A), .in1(B), .in2(C));
  NotExactlyOne xnor_1 (.out(ODD___A_XNOR_B_XNOR_C), .in0(A), .in1(B), .in2(C));

  // Notes on the sheet:
  //   Name - Debarghaya Mitra        Enrollment Number - 12024052002215        Branch - CSE        Section - C        Roll No - 248
  //   Assignment - 16
  //   Parity Generator
endmodule
