// Logisim project Assignment 2.circ as structural Verilog: 1 circuit, main circuit main
module main (
  input  A,
  input  B,
  input  A_2,
  input  B_2,
  output out_5,
  output out_6
);

  wire and_1_out, and_2_out, and_3_out, and_4_out, and_5_out, nand_1_out, not_1_out, not_2_out, not_3_out,
       or_1_out, or_2_out, or_3_out, xor_1_out;

  not not_1 (not_1_out, A_2);
  not not_2 (not_2_out, B_2);
  and and_1 (and_1_out, not_1_out, B_2);
  and and_2 (and_2_out, not_2_out, A_2);
  xor xor_1 (xor_1_out, B, A);
  nand nand_1 (nand_1_out, B, A);
  or or_1 (or_1_out, B, A);
  and and_3 (and_3_out, B_2, A_2);
  or or_2 (or_2_out, B_2, A_2);
  or or_3 (or_3_out, and_1_out, and_2_out);
  not not_3 (not_3_out, and_3_out);
  and and_4 (and_4_out, xor_1_out, nand_1_out);
  and and_5 (and_5_out, or_3_out, not_3_out);
  or or_4 (out_5, and_4_out, or_1_out);
  or or_5 (out_6, and_5_out, or_2_out);

  // Notes on the sheet:
  //   Using Minimum Number of Gates
  //   Using Basic Gates
  //   Name - Debarghaya Mitra            Enrollment Number - 12024052002215            Branch - CSE                Section - C                Roll No - 248
  //   Assignment - 2
  //   Y = [(A'B + B'A)(AB)'] + (A + B)
  //   Y = [(A'B + B'A)(AB)'] + (A + B)
endmodule
