// Logisim project Assignment 5.circ as structural Verilog: 1 circuit, main circuit main
module main (
  input  A,
  input  B,
  input  C,
  input  D,
  output F___A_prime_B_prime_C___A_prime_BD___AD_B_prime_C___BC_prime
);

  wire and_1_out, and_2_out, and_3_out, not_1_out, not_2_out, xor_1_out;

  not not_1 (not_1_out, A);
  not not_2 (not_2_out, B);
  xor xor_1 (xor_1_out, B, C);
  and and_1 (and_1_out, not_1_out, not_2_out, C);
  and and_2 (and_2_out, not_1_out, B, D);
  and and_3 (and_3_out, A, D, xor_1_out);
  or or_1 (F___A_prime_B_prime_C___A_prime_BD___AD_B_prime_C___BC_prime, and_1_out, and_2_out, and_3_out);

  // Notes on the sheet:
  //   A'
  //   B'
  //   B'C + BC'
  //   A'B'C
  //   A'BD
  //   AD(B'C + BC')
  //   Name - Debarghaya Mitra        Enrollment Number - 12024052002215        Branch - CSE        Section - C        Roll No - 248
  //   Assignment - 5
endmodule
