// Logisim project Assignment 6.circ as structural Verilog: 1 circuit, main circuit main
module main (
  input  A,
  input  A_2,
  input  B,
  input  A_3,
  input  B_2,
  input  A_4,
  input  B_3,
  input  B_4,
  input  A_5,
  input  A_6,
  output F___AB,
  output F___AB_2,
  output F___A___B,
  output F___A___B_2,
  output F___A_prime,
  output F___A_prime_2
);

  wire nand_1_out, nand_2_out, nand_3_out, nor_1_out, nor_2_out, nor_3_out;

  nand nand_1 (nand_1_out, A, B);
  nand nand_2 (nand_2_out, A_3, A_3);
  nand nand_3 (nand_3_out, B_3, B_3);
  nand nand_4 (F___A_prime, A_5, A_5);
  nand nand_5 (F___AB, nand_1_out, nand_1_out);
  nand nand_6 (F___A___B, nand_2_out, nand_3_out);
  nor nor_1 (nor_1_out, A_2, A_2);
  nor nor_2 (nor_2_out, B_2, B_2);
  nor nor_3 (nor_3_out, A_4, B_4);
  nor nor_4 (F___A_prime_2, A_6, A_6);
  nor nor_5 (F___AB_2, nor_1_out, nor_2_out);
  nor nor_6 (F___A___B_2, nor_3_out, nor_3_out);

  // Notes on the sheet:
  //   AND Gate using NAND Gate
  //   OR Gate using NAND Gate
  //   AND Gate using NAND Gate
  //   Name - Debarghaya Mitra        Enrollment Number - 12024052002215        Branch - CSE        Section - C        Roll No - 248
  //   Assignment - 6
  //   OR Gate using NOR Gate
  //   AND Gate using NOR Gate
  //   OR Gate using NOR Gate
endmodule
