// Logisim project Assignment 8.circ as structural Verilog: 1 circuit, main circuit main
module main (
  input  A,
  input  B,
  input  A_2,
  input  B_2,
  input  A_3,
  input  B_3,
  input  C,
  input  A_4,
  input  B_4,
  input  C_2,
  output Sum,
  output Sum_2,
  output Carry,
  output Carry_2,
  output Sum_3,
  output Sum_4,
  output Carry_3,
  output Carry_4
);

  wire and_1_out, and_2_out, and_4_out, and_5_out, and_6_out, and_7_out, and_8_out, and_9_out, and_11_out,
       and_12_out, not_1_out, not_2_out, not_3_out, not_4_out, not_5_out, not_6_out, or_2_out, xor_2_out;

  not not_1 (not_1_out, A_2);
  not not_2 (not_2_out, B_2);
  not not_3 (not_3_out, A_4);
  not not_4 (not_4_out, B_4);
  and and_1 (and_1_out, B_2, not_1_out);
  and and_2 (and_2_out, not_2_out, A_2);
  and and_3 (Carry_2, B_2, A_2);
  and and_4 (and_4_out, B_4, not_3_out);
  and and_5 (and_5_out, not_4_out, A_4);
  and and_6 (and_6_out, B_4, A_4);
  or or_1 (Sum_2, and_1_out, and_2_out);
  or or_2 (or_2_out, and_4_out, and_5_out);
  not not_5 (not_5_out, or_2_out);
  not not_6 (not_6_out, C_2);
  and and_7 (and_7_out, not_5_out, C_2);
  and and_8 (and_8_out, or_2_out, not_6_out);
  and and_9 (and_9_out, or_2_out, C_2);
  or or_3 (Sum_4, and_7_out, and_8_out);
  or or_4 (Carry_4, and_9_out, and_6_out);
  xor xor_1 (Sum, A, B);
  and and_10 (Carry, B, A);
  and and_11 (and_11_out, B_3, A_3);
  xor xor_2 (xor_2_out, A_3, B_3);
  xor xor_3 (Sum_3, xor_2_out, C);
  and and_12 (and_12_out, xor_2_out, C);
  or or_5 (Carry_3, and_12_out, and_11_out);

  // Notes on the sheet:
  //   Half Adder using Basic Gates
  //   Full Adder using Half Adders
  //   Name - Debarghaya Mitra        Enrollment Number - 12024052002215        Branch - CSE        Section - C        Roll No - 248
  //   Assignment - 8
  //   Half Adder using Minimum Number of Gates
  //   Full Adder using Minimum Number of Gates
endmodule
