// Logisim project Assignment 9.circ as structural Verilog: 1 circuit, main circuit main
module main (
  input  A,
  input  B,
  input  A_2,
  input  B_2,
  input  A_3,
  input  B_3,
  input  A_4,
  input  B_4,
  input  C,
  input  C_2,
  output Difference,
  output Difference_2,
  output Borrow,
  output Borrow_2,
  output Difference_3,
  output Borrow_3,
  output Difference_4,
  output Borrow_4
);

  wire and_2_out, and_3_out, and_4_out, and_5_out, and_6_out, and_7_out, and_8_out, and_9_out, and_11_out,
       and_12_out, not_1_out, not_2_out, not_3_out, not_4_out, not_5_out, not_6_out, not_7_out, not_8_out,
       not_9_out, not_10_out, or_1_out, xor_2_out;

  not not_1 (not_1_out, A);
  not not_2 (not_2_out, A_3);
  xor xor_1 (Difference, B, A);
  and and_1 (Borrow, B, not_1_out);
  not not_3 (not_3_out, B_3);
  and and_2 (and_2_out, not_2_out, B_3);
  and and_3 (and_3_out, not_3_out, A_3);
  and and_4 (and_4_out, not_2_out, B_3);
  or or_1 (or_1_out, and_2_out, and_3_out);
  not not_4 (not_4_out, or_1_out);
  not not_5 (not_5_out, or_1_out);
  and and_5 (and_5_out, not_5_out, C_2);
  and and_6 (and_6_out, or_1_out, not_6_out);
  not not_6 (not_6_out, C_2);
  and and_7 (and_7_out, not_4_out, C_2);
  or or_2 (Borrow_4, and_7_out, and_4_out);
  or or_3 (Difference_4, and_5_out, and_6_out);
  not not_7 (not_7_out, A_2);
  not not_8 (not_8_out, B_2);
  and and_8 (and_8_out, not_7_out, B_2);
  and and_9 (and_9_out, not_8_out, A_2);
  and and_10 (Borrow_2, not_7_out, B_2);
  not not_9 (not_9_out, A_4);
  xor xor_2 (xor_2_out, A_4, B_4);
  or or_4 (Difference_2, and_8_out, and_9_out);
  xor xor_3 (Difference_3, xor_2_out, C);
  not not_10 (not_10_out, xor_2_out);
  and and_11 (and_11_out, not_10_out, C);
  and and_12 (and_12_out, not_9_out, B_4);
  or or_5 (Borrow_3, and_11_out, and_12_out);

  // Notes on the sheet:
  //   Half Subtractor using Minimum Number of Gates
  //   Full Subtractor using Half Subtractors
  //   Name - Debarghaya Mitra        Enrollment Number - 12024052002215        Branch - CSE        Section - C        Roll No - 248
  //   Assignment - 9
  //   Half Subtractor using Basic Gates
  //   Full Subtractor using Minimum Number of Gates
endmodule
